// Logisim project state_machine_diagram.circ as structural Verilog: 1 circuit, main circuit main
module main (
  input  v,
  input  v0,
  input  a,
  input  F
);

  wire [7:0] multiplier_1_out, multiplier_2_out, multiplier_3_out, subtractor_1_out;
  wire [7:1] undriven, undriven_2, undriven_3;

  Multiplier multiplier_1 (.a({undriven, v}), .b({undriven, v}), .out(multiplier_1_out));  // open: cin, cout
  Multiplier multiplier_2 (.a({undriven_2, v0}), .b({undriven_2, v0}), .out(multiplier_2_out));  // open: cin, cout
  Multiplier multiplier_3 (.a({undriven_3, a}), .b(8'h2), .out(multiplier_3_out));  // open: cin, cout
  Subtractor subtractor_1 (.a(multiplier_1_out), .b(multiplier_2_out), .out(subtractor_1_out));  // open: bin, bout
  Demultiplexer demultiplexer_1 ();  // open: out0, out1, in, sel, en
  Divider divider_1 (.a(subtractor_1_out), .b(multiplier_3_out));  // open: out, upper, rem
  Multiplexer #(.select(2)) multiplexer_1 ();  // open: in0, in1, in2, in3, out, sel, en
  Decoder #(.select(2)) decoder_1 ();  // open: out0, out1, out2, out3, sel, en
  Counter #(.width(2), .max('h3)) counter_1 ();  // open: load, D, count, Q, carry, clk, clr
  // Pins of 1 and 8 bits meet at {undriven_2, v0}
  // Pins of 1 and 8 bits meet at {undriven, v}
  // Pins of 1 and 8 bits meet at {undriven_3, a}
endmodule
